# Fritzing sketch Branchement (saved by Fritzing 0.9.3b)
breadboards: 1

parts:
  L298N1 = L298N DC motor driver
  M1 = DC Motor
  rd = NRF24L01+ Breakout Board
  Composant6 = Arduino Nano (Rev3.0)
  Composant8 = NRF24L01+ Breakout Board
  S1 = Pushbutton [package="[THT]"]
  Composant1 = Arduino Uno (Rev3)
  VCC4 = Battery block 9V
  S2 = Pushbutton [package="[THT]"]
  VCC3 = Battery block 9V

nets:
  N1: L298N1.OUT1, M1.pin_2
  N2: L298N1.OUT2, M1.pin_1
  GND: L298N1.GND, Composant6.GND, VCC3.-
  N3: L298N1.ENA, Composant6.D6
  N4: L298N1.IN1, Composant6.D5
  N5: L298N1.IN2, Composant6.D4
  VCC: rd.VCC, Composant6.3V3
  N6: rd.CE, Composant6.D9
  N7: rd.CS, Composant6.D10
  N8: rd.SCK, Composant6.D13/SCK
  N9: rd.MOSI, Composant6.D11/MOSI
  N10: rd.MISO, Composant6.D12/MISO
  N11: Composant6.VIN, VCC3.+
  GND_2: Composant8.GND, S1.Pin_1, S1.Pin_2, Composant1.GND, Composant1.D7, S2.Pin_1, S2.Pin_2
  VCC_2: Composant8.VCC, Composant1.3V3
  N12: Composant8.CE, Composant1.D9_PWM
  N13: Composant8.CS, Composant1.D10_PWM/SS
  N14: Composant8.SCK, Composant1.D13/SCK
  N15: Composant8.MOSI, Composant1.D11_PWM/MOSI
  N16: Composant8.MISO, Composant1.D12/MISO
  N17: S1.Pin_3, S1.Pin_4
  N18: Composant1.D8, S2.Pin_3, S2.Pin_4
  N19: Composant1.5V, VCC4.+

custom parts:
  L298N DC motor driver: 2x DC motor driver with 78M05 positive voltage regulator (7..35 V) L298N: max 46 V, 2 A Set 5 V Enable jumper to enable 5 V regultor (needed for the L298N) and +5 V output at screw terminal or supply external +5 V at screw terminal Set ENA and/or ENB to +5 V to enable motor permanently or supply ENA and/or ENB with PWM signal IN1 and IN2 set rotation directory for motor A (OUT1/OUT2) IN2 and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
